# Fritzing sketch fys_project (saved by Fritzing 0.9.10b)
breadboards: 1

parts:
  J1 = Basic Servo
  HC-SR04_Sensor_1 = HC-SR04 Ultrasonic Distance Sensor
  SOUND_SENSOR = Dagu DGServo 9g header connector (female) [package=THT]
  Mod1 = KY-008 Laser Transmitter Module [package="Breakout board"]
  Mod2 = KY-018 Photoresistor Module [package="Breakout board"]
  Part1 = ODROID-N2Plus [part_number="ODROID N2Plus"]
  Mod3 = KY-026 Flame Sensor Module [package="Breakout board"]

nets:
  GND: J1.gnd, HC-SR04_Sensor_1.GND, SOUND_SENSOR.gnd, Mod1.NC, Mod1.-, Mod2.-, Part1.connector6
  VCC: J1.vcc, HC-SR04_Sensor_1.VCC, SOUND_SENSOR.Vcc, Mod1.S, Part1.connector2, Mod3.G, Mod3.+
  N1: J1.pulse, Part1.connector14
  N2: HC-SR04_Sensor_1.TRIG, Part1.connector7
  N3: HC-SR04_Sensor_1.ECHO, Part1.connector11
  N4: SOUND_SENSOR.pulse, Part1.connector37
  N5: Mod2.S, Part1.connector5
  N6: Mod2.Vin, Part1.connector1
  N7: Part1.connector40, Mod3.A0

custom parts:
  KY-008 Laser Transmitter Module: KY-008 Laser Transmitter Module, emits a dot shaped red laser beam.
  KY-018 Photoresistor Module: KY-018 Photoresistor module, used to measure light intensity. It can determine the presence or absence of light.
  KY-026 Flame Sensor Module: KY-026 Flame Sensor Module reacts in the presence of fire.
